# Fritzing sketch Placa_1 (saved by Fritzing 0.9.3b)
circuit board: 17.9951cm x 5.05871cm
breadboards: 3

parts:
  Entrada_de_datos_y_5_voltios_spark = screw terminal, 5 pins
  U1 = 74HC595 [package="DIP16 [THT]"]
  U2 = 74HC595 [package="DIP16 [THT]"]
  U3 = 74HC595 [package="DIP16 [THT]"]
  U4 = 74HC595 [package="DIP16 [THT]"]
  Q1 = npn-Powertransistor [package="TO220 [THT]"]
  Q2 = npn-Powertransistor [package="TO220 [THT]"]
  Q3 = npn-Powertransistor [package="TO220 [THT]"]
  Q4 = npn-Powertransistor [package="TO220 [THT]"]
  Q5 = npn-Powertransistor [package="TO220 [THT]"]
  Q6 = npn-Powertransistor [package="TO220 [THT]"]
  Q7 = npn-Powertransistor [package="TO220 [THT]"]
  Q8 = npn-Powertransistor [package="TO220 [THT]"]
  Q9 = npn-Powertransistor [package="TO220 [THT]"]
  Q10 = npn-Powertransistor [package="TO220 [THT]"]
  Q11 = npn-Powertransistor [package="TO220 [THT]"]
  Q12 = npn-Powertransistor [package="TO220 [THT]"]
  Q13 = npn-Powertransistor [package="TO220 [THT]"]
  Q14 = npn-Powertransistor [package="TO220 [THT]"]
  Q15 = npn-Powertransistor [package="TO220 [THT]"]
  Q16 = npn-Powertransistor [package="TO220 [THT]"]
  Q17 = npn-Powertransistor [package="TO220 [THT]"]
  Q18 = npn-Powertransistor [package="TO220 [THT]"]
  Q19 = npn-Powertransistor [package="TO220 [THT]"]
  Q20 = npn-Powertransistor [package="TO220 [THT]"]
  Q21 = npn-Powertransistor [package="TO220 [THT]"]
  Q30 = npn-Powertransistor [package="TO220 [THT]"]
  Q23 = npn-Powertransistor [package="TO220 [THT]"]
  Q27 = npn-Powertransistor [package="TO220 [THT]"]
  Q29 = npn-Powertransistor [package="TO220 [THT]"]
  Q28 = npn-Powertransistor [package="TO220 [THT]"]
  Q22 = npn-Powertransistor [package="TO220 [THT]"]
  Q24 = npn-Powertransistor [package="TO220 [THT]"]
  Q25 = npn-Powertransistor [package="TO220 [THT]"]
  Q26 = npn-Powertransistor [package="TO220 [THT]"]
  Q31 = npn-Powertransistor [package="TO220 [THT]"]
  Q32 = npn-Powertransistor [package="TO220 [THT]"]
  D1 = Diode [package=diode-1n4148]
  D2 = Diode [package=diode-1n4148]
  D3 = Diode [package=diode-1n4148]
  D4 = Diode [package=diode-1n4148]
  D5 = Diode [package=diode-1n4148]
  D6 = Diode [package=diode-1n4148]
  D7 = Diode [package=diode-1n4148]
  D8 = Diode [package=diode-1n4148]
  D9 = Diode [package=diode-1n4148]
  D10 = Diode [package=diode-1n4148]
  D11 = Diode [package=diode-1n4148]
  D12 = Diode [package=diode-1n4148]
  D13 = Diode [package=diode-1n4148]
  D14 = Diode [package=diode-1n4148]
  D15 = Diode [package=diode-1n4148]
  D16 = Diode [package=diode-1n4148]
  D17 = Diode [package=diode-1n4148]
  D18 = Diode [package=diode-1n4148]
  D19 = Diode [package=diode-1n4148]
  D20 = Diode [package=diode-1n4148]
  D21 = Diode [package=diode-1n4148]
  D22 = Diode [package=diode-1n4148]
  D23 = Diode [package=diode-1n4148]
  D24 = Diode [package=diode-1n4148]
  D25 = Diode [package=diode-1n4148]
  D26 = Diode [package=diode-1n4148]
  D27 = Diode [package=diode-1n4148]
  D28 = Diode [package=diode-1n4148]
  D29 = Diode [package=diode-1n4148]
  D30 = Diode [package=diode-1n4148]
  D31 = Diode [package=diode-1n4148]
  D32 = Diode [package=diode-1n4148]
  L31 = Solenoid
  L29 = Solenoid
  L27 = Solenoid
  L25 = Solenoid
  L21 = Solenoid
  L23 = Solenoid
  L19 = Solenoid
  L15 = Solenoid
  L13 = Solenoid
  L17 = Solenoid
  L11 = Solenoid
  L9 = Solenoid
  L7 = Solenoid
  L5 = Solenoid
  L3 = Solenoid
  L1 = Solenoid
  L32 = Solenoid
  L30 = Solenoid
  L28 = Solenoid
  L26 = Solenoid
  L24 = Solenoid
  L22 = Solenoid
  L20 = Solenoid
  L18 = Solenoid
  L16 = Solenoid
  L14 = Solenoid
  L12 = Solenoid
  L10 = Solenoid
  L8 = Solenoid
  L6 = Solenoid
  L4 = Solenoid
  L2 = Solenoid
  Alimentacion_12v-solenoides = Screw terminal - 2 pins [package=THT]
  Salida_de_datos_y_de_voltaje_5v = screw terminal, 5 pins
  salida_12_voltios_siguiente_tarjeta = Screw terminal - 2 pins [package=THT]

nets:
  N1: Entrada_de_datos_y_5_voltios_spark.pin1, U1.DS
  N2: Entrada_de_datos_y_5_voltios_spark.pin2, U1.SH_CP, U2.SH_CP, U3.SH_CP, U4.SH_CP, Salida_de_datos_y_de_voltaje_5v.pin4
  N3: Entrada_de_datos_y_5_voltios_spark.pin3, U1.ST_CP, U2.ST_CP, U3.ST_CP, U4.ST_CP, Salida_de_datos_y_de_voltaje_5v.pin3
  VCC: Entrada_de_datos_y_5_voltios_spark.pin4, U1.MR, U1.VCC, U2.MR, U2.VCC, U3.MR, U3.VCC, U4.MR, U4.VCC, Salida_de_datos_y_de_voltaje_5v.pin1
  GND: Entrada_de_datos_y_5_voltios_spark.pin5, U1.GND, U1.OE, U2.GND, U2.OE, U3.GND, U3.OE, U4.GND, U4.OE, Q1.emitter, Q2.emitter, Q3.emitter, Q4.emitter, Q5.emitter, Q6.emitter, Q7.emitter, Q8.emitter, Q9.emitter, Q10.emitter, Q11.emitter, Q12.emitter, Q13.emitter, Q14.emitter, Q15.emitter, Q16.emitter, Q17.emitter, Q18.emitter, Q19.emitter, Q20.emitter, Q21.emitter, Q30.emitter, Q23.emitter, Q27.emitter, Q29.emitter, Q28.emitter, Q22.emitter, Q24.emitter, Q25.emitter, Q26.emitter, Q31.emitter, Q32.emitter, L31.pin1, L29.pin1, L27.pin1, L25.pin1, L21.pin1, L23.pin1, L19.pin1, L15.pin1, L13.pin1, L17.pin1, L11.pin1, L9.pin1, L7.pin1, L5.pin1, L3.pin1, L1.pin1, L32.pin1, L30.pin1, L28.pin1, L26.pin1, L24.pin1, L22.pin1, L20.pin1, L18.pin1, L16.pin1, L14.pin1, L12.pin1, L10.pin1, L8.pin1, L6.pin1, L4.pin1, L2.pin1, Alimentacion_12v-solenoides.pin1, Salida_de_datos_y_de_voltaje_5v.pin2, salida_12_voltios_siguiente_tarjeta.pin2
  N4: U1.Q1, Q2.base
  N5: U1.Q2, Q3.base
  N6: U1.Q3, Q4.base
  N7: U1.Q4, Q5.base
  N8: U1.Q5, Q6.base
  N9: U1.Q6, Q7.base
  N10: U1.Q7, Q8.base
  N11: U1.Q7', U2.DS
  N12: U1.Q0, Q1.base
  N13: U2.Q1, Q10.base
  N14: U2.Q2, Q11.base
  N15: U2.Q3, Q12.base
  N16: U2.Q4, Q13.base
  N17: U2.Q5, Q14.base
  N18: U2.Q6, Q15.base
  N19: U2.Q7, Q16.base
  N20: U2.Q7', U3.DS
  N21: U2.Q0, Q9.base
  N22: U3.Q1, Q18.base
  N23: U3.Q2, Q19.base
  N24: U3.Q3, Q20.base
  N25: U3.Q4, Q21.base
  N26: U3.Q5, Q22.base
  N27: U3.Q6, Q23.base
  N28: U3.Q7, Q24.base
  N29: U3.Q7', U4.DS
  N30: U3.Q0, Q17.base
  N31: U4.Q1, Q26.base
  N32: U4.Q2, Q27.base
  N33: U4.Q3, Q28.base
  N34: U4.Q4, Q29.base
  N35: U4.Q5, Q30.base
  N36: U4.Q6, Q31.base
  N37: U4.Q7, Q32.base
  N38: U4.Q7', Salida_de_datos_y_de_voltaje_5v.pin5
  N39: U4.Q0, Q25.base
  N40: Q1.collector, D1.A
  N41: D1.C, D2.C, D3.C, D4.C, D5.C, D6.C, D7.C, D8.C, D9.C, D10.C, D11.C, D12.C, D13.C, D14.C, D15.C, D16.C, D17.C, D18.C, D19.C, D20.C, D21.C, D22.C, D23.C, D24.C, D25.C, D26.C, D27.C, D28.C, D29.C, D30.C, D31.C, D32.C, L31.pin2, L29.pin2, L27.pin2, L25.pin2, L21.pin2, L23.pin2, L19.pin2, L15.pin2, L13.pin2, L17.pin2, L11.pin2, L9.pin2, L7.pin2, L5.pin2, L3.pin2, L32.pin2, L30.pin2, L28.pin2, L26.pin2, L24.pin2, L22.pin2, L20.pin2, L18.pin2, L16.pin2, L14.pin2, L12.pin2, L10.pin2, L8.pin2, L6.pin2, L4.pin2, L2.pin2, Alimentacion_12v-solenoides.pin2, salida_12_voltios_siguiente_tarjeta.pin1
