# Fritzing sketch Placa_cerebro (saved by Fritzing 0.9.3b)
circuit board: 16.9689cm x 10.9369cm
breadboards: 2

parts:
  ESP38pin = ESP32-38PinWide [part_number=ESP32-38PinWide]
  Pro_Micro1 = SparkFun Pro Micro
  M1 = RioRand LM2596
  C1 = Capacitor Polarized [package=cpol-radial-100uf-25v]
  Pro_Micro2 = SparkFun Pro Micro
  S1 = Momentary Switch [package=ksa_sealed_tac_switch]
  S2 = Momentary Switch [package=ksa_sealed_tac_switch]
  S3 = Momentary Switch [package=ksa_sealed_tac_switch]
  S4 = Momentary Switch [package=ksa_sealed_tac_switch]
  Reset = Momentary Switch [package=ksa_sealed_tac_switch]
  R1 = Resistor [tolerance=±5% resistance=10k package=THT]
  R2 = Resistor [tolerance=±5% resistance=10k package=THT]
  R3 = Resistor [tolerance=±5% resistance=10k package=THT]
  R4 = Resistor [tolerance=±5% resistance=10k package=THT]
  Rreset = Resistor [tolerance=±5% resistance=10k package=THT]
  Pot = POT [package=alps_pot]
  LCD = LCD1602-I2C
  Salida_de_datos_a_RC = screw terminal, 3 pins
  Salida_de_5_voltios = screw terminal, 2 pins
  Entrada_y_salida_de_12_voltios = screw terminal, 4 pins

nets:
  GND: ESP38pin.GPIO11, Pro_Micro1.GND, M1.Pin_4, C1.-, Pro_Micro2.GND, R1.Pin_1, R2.Pin_1, R3.Pin_1, R4.Pin_1, Rreset.Pin_1, Pot.E, LCD.GND, Salida_de_5_voltios.pin2
  VCC: ESP38pin.VIN, Pro_Micro1.A1, Pro_Micro1.RAW, M1.Pin_3, C1.+, Pro_Micro2.TX0, Pro_Micro2.VCC, Pro_Micro2.RAW, S1.3, S2.3, S3.3, S4.3, Reset.3, Pot.A, LCD.VCC, Salida_de_5_voltios.pin1
  N1: ESP38pin.GPIO3, Pro_Micro2.RX1
  N2: ESP38pin.GPIO1, Pro_Micro1.RX1
  N3: Pro_Micro1.16, Salida_de_datos_a_RC.pin3
  N4: Pro_Micro1.15, Salida_de_datos_a_RC.pin2
  N5: Pro_Micro1.A0, Salida_de_datos_a_RC.pin1
  N6: M1.Pin_1, Entrada_y_salida_de_12_voltios.pin3, Entrada_y_salida_de_12_voltios.pin4
  N7: M1.Pin_2, Entrada_y_salida_de_12_voltios.pin1, Entrada_y_salida_de_12_voltios.pin2
  N8: Pro_Micro2.2, LCD.SDA
  N9: Pro_Micro2.3, LCD.SCL
  N10: Pro_Micro2.4, S3.2, R3.Pin_0
  N11: Pro_Micro2.5, S1.2, R1.Pin_0
  N12: Pro_Micro2.6, S2.2, R2.Pin_0
  N13: Pro_Micro2.7, S4.2, R4.Pin_0
  N14: Pro_Micro2.8, Reset.2, Rreset.Pin_0
  N15: Pro_Micro2.10, Pot.S

custom parts:
  ESP32-38PinWide: Generic 38-Pin ESP32 with wide format (only access to one side of pins on a breadboard) based on Stephen Lilley's HiLetgo ESP-WROOM-32 ESP32 ESP-32S Development Board.
  SparkFun Pro Micro: The Pro Micro is similar to the Pro Mini except with an ATmega32U4 on board. The USB transceiver inside the 32U4 allows us to add USB connectivity on-board and do away with bulky external USB interface. Based on: https://github.com/unorthodox-engineers/unorthodox-arduino/blob/master/Unorthodox/fritzing/parts/Pro%20Micro.fzpz
  LCD1602-I2C: A standard character display, usually with 2x16 characters. Comes in many colors with LCM1602 IIC attached.
